# Fritzing sketch Arduino GPS Satellite (saved by Fritzing 0.9.7b)

parts:
  Part1 = Arduino Uno (Rev3)
  R1 = Resistor [tolerance=±5% power=0.25 resistance=10 package=THT]
  LED1 = LED - 3mm [color="Red (633nm)" current=0.030 package="3 mm [THT]"]
  R2 = Resistor [tolerance=±5% power=0.25 resistance=10k package=THT]
  U3 = SPDT Slide Switch [package=ayz0202]  # not connected
  ANT1 = Antenna  # not connected
  U4 = ESP8266 WiFi Module [part_number=ESP8266]
  LED2 = LED - 3mm [color="Green (555nm)" current=0.030 package="3 mm [THT]"]
  R3 = Temperature Sensor (Thermistor) [thermistor_type=NTC package=THT]
  R4 = Resistor [tolerance=±5% power=0.25 resistance=220 package=THT]
  Part2 = Memoire 1.0 - SD card log shield

nets:
  N1: Part1.A0, R3.pin_0
  N2: Part1.A4/SDA, Part2.A_IN_4
  N3: Part1.A5/SCL, Part2.A_IN_5
  GND: Part1.GND, LED1.anode, R4.Pin_1, Part2.GND
  N4: Part1.D0/RX, U4.RX
  N5: Part1.D1/TX, U4.TX
  N6: Part1.D6_PWM, R2.Pin_0
  N7: Part1.D7, R1.Pin_0
  5V: Part1.5V, U4.3.3V#26, Part2.+5V
  N8: R2.Pin_1, LED2.cathode
  N9: U4.GND, LED2.anode
  N10: R3.pin_1, R4.Pin_0

notes:
  KIM1 Satellite
